# Fritzing sketch Gatekeeper (saved by Fritzing 0.9.4)
breadboards: 1

parts:
  J1 = Piezo Speaker  # not connected
  U1 = ESP8266 NodeMCU LoLin module
  M1 = fc-51 [package=THT]

nets:
  N1: U1.3V3, M1.pin3
  N2: U1.GND, M1.pin2
  N3: U1.D5, M1.pin1

custom parts:
  ESP8266 NodeMCU LoLin module: ESP8266 based NodeMCU
